// Logisim project cacheMemory.circ as structural Verilog: 3 circuits, main circuit Cache
module Cache (
  input  [31:0] W0_write,
  input  [31:0] W1_write,
  input  [31:0] W2_write,
  input  [31:0] W3_write,
  input  [9:0] Tag_writeAndRead,
  input  clk,
  input  [1:0] word_read,
  input  [1:0] SetBit_writeAndRead,
  output [31:0] BlockWord
);

  wire demultiplexer_1_out0, demultiplexer_1_out1, demultiplexer_1_out2, demultiplexer_1_out3;
  wire [31:0] set_1_blockword, set_2_blockword, set_3_blockword, set_4_blockword;

  Demultiplexer #(.select(2)) demultiplexer_1 (
    .out0(demultiplexer_1_out0), .out1(demultiplexer_1_out1), .out2(demultiplexer_1_out2),
    .out3(demultiplexer_1_out3), .in(1'b1), .sel(SetBit_writeAndRead));
  SET set_1 (
    .W0_write(W0_write), .W1_write(W1_write), .W2_write(W2_write), .W3_write(W3_write), .clk(clk),
    .Word_read(word_read), .Tag_writeAndRead(Tag_writeAndRead), .writeEnable(demultiplexer_1_out0),
    .BlockWord(set_1_blockword));  // open: miss
  SET set_2 (
    .W0_write(W0_write), .W1_write(W1_write), .W2_write(W2_write), .W3_write(W3_write), .clk(clk),
    .Word_read(word_read), .Tag_writeAndRead(Tag_writeAndRead), .writeEnable(demultiplexer_1_out1),
    .BlockWord(set_2_blockword));  // open: miss
  SET set_3 (
    .W0_write(W0_write), .W1_write(W1_write), .W2_write(W2_write), .W3_write(W3_write), .clk(clk),
    .Word_read(word_read), .Tag_writeAndRead(Tag_writeAndRead), .writeEnable(demultiplexer_1_out2),
    .BlockWord(set_3_blockword));  // open: miss
  SET set_4 (
    .W0_write(W0_write), .W1_write(W1_write), .W2_write(W2_write), .W3_write(W3_write), .clk(clk),
    .Word_read(word_read), .Tag_writeAndRead(Tag_writeAndRead), .writeEnable(demultiplexer_1_out3),
    .BlockWord(set_4_blockword));  // open: miss
  Multiplexer #(.select(2), .width(32)) multiplexer_1 (
    .in0(set_1_blockword), .in1(set_2_blockword), .in2(set_3_blockword), .in3(set_4_blockword),
    .out(BlockWord), .sel(SetBit_writeAndRead));

  // Other names for the same wires on the sheet: tag[9:0] = Tag_writeAndRead; W0[31:0] = W0_write;
  //   W1[31:0] = W1_write; W2[31:0] = W2_write; W3[31:0] = W3_write; word[1:0] = word_read
endmodule

module BLOCK_4x32 (
  input  [31:0] W0_write,
  input  [31:0] W1_write,
  input  [31:0] W2_write,
  input  [31:0] W3_write,
  input  clk,
  input  [1:0] Word_read,
  input  [9:0] Tag_write,
  input  V,
  input  Enable,
  output [31:0] BlockWord,
  output [9:0] BlockTag,
  output validBit
);

  wire [31:0] register_1_q, register_2_q, register_3_q, register_4_q;

  Register #(.width(32)) register_1 (.D(W0_write), .en(Enable), .clk(clk), .Q(register_1_q));  // open: clr
  Register #(.width(32)) register_2 (.D(W1_write), .en(Enable), .clk(clk), .Q(register_2_q));  // open: clr
  Register #(.width(32)) register_3 (.D(W2_write), .en(Enable), .clk(clk), .Q(register_3_q));  // open: clr
  Register #(.width(32)) register_4 (.D(W3_write), .en(Enable), .clk(clk), .Q(register_4_q));  // open: clr
  Register #(.width(10)) register_5 (.D(Tag_write), .en(Enable), .clk(clk), .Q(BlockTag));  // open: clr
  Register #(.width(1)) register_6 (.D(V), .en(Enable), .clk(clk), .Q(validBit));  // open: clr
  Multiplexer #(.select(2), .width(32)) multiplexer_1 (
    .in0(register_1_q), .in1(register_2_q), .in2(register_3_q), .in3(register_4_q), .out(BlockWord),
    .sel(Word_read));

  // Notes on the sheet:
  //   when enable is 1 and v is 1 we should write back in memory
endmodule

module SET (
  input  [31:0] W0_write,
  input  [31:0] W1_write,
  input  [31:0] W2_write,
  input  [31:0] W3_write,
  input  clk,
  input  [1:0] Word_read,
  input  [9:0] Tag_writeAndRead,
  input  writeEnable,
  output [31:0] BlockWord,
  output miss
);

  wire and_1_out, and_2_out, clk_t, comparator_1_eq, comparator_2_eq, enable, v1, v2;
  wire [9:0] blockTag1, blockTag2;
  wire [31:0] block_4x32_1_blockword, block_4x32_2_blockword;

  T_Flip_Flop t_ff_1 (.T(1'b1), .clk(clk_t), .Q(enable));  // open: Qn, reset, preset
  Multiplexer multiplexer_1 (.in0(1'b0), .in1(clk), .out(clk_t), .sel(writeEnable));
  BLOCK_4x32 block_4x32_1 (
    .W0_write(W0_write), .W1_write(W1_write), .W2_write(W2_write), .W3_write(W3_write), .clk(clk_t),
    .Word_read(Word_read), .Tag_write(Tag_writeAndRead), .V(1'b1), .Enable(enable),
    .BlockWord(block_4x32_1_blockword), .BlockTag(blockTag1), .validBit(v1));
  BLOCK_4x32 block_4x32_2 (
    .W0_write(W0_write), .W1_write(W1_write), .W2_write(W2_write), .W3_write(W3_write), .clk(clk_t),
    .Word_read(Word_read), .Tag_write(Tag_writeAndRead), .V(1'b1), .Enable(enable),
    .BlockWord(block_4x32_2_blockword), .BlockTag(blockTag2), .validBit(v2));
  Comparator #(.width(10)) comparator_1 (.a(blockTag1), .b(Tag_writeAndRead), .eq(comparator_1_eq));  // open: gt, lt
  Comparator #(.width(10)) comparator_2 (.a(Tag_writeAndRead), .b(blockTag2), .eq(comparator_2_eq));  // open: gt, lt
  and and_1 (and_1_out, v1, comparator_1_eq);
  and and_2 (and_2_out, comparator_2_eq, v2);
  Multiplexer #(.enable("true"), .width(32)) multiplexer_2 (
    .in0(block_4x32_1_blockword), .in1(block_4x32_2_blockword), .out(BlockWord), .sel(and_2_out), .en(miss));
  nor nor_1 (miss, and_1_out, and_2_out);

  // Other names for the same wires on the sheet: tag[9:0] = Tag_writeAndRead; W0[31:0] = W0_write;
  //   W1[31:0] = W1_write; W2[31:0] = W2_write; W3[31:0] = W3_write; word[1:0] = Word_read

  // Notes on the sheet:
  //   if 1 miss
endmodule
