// Logisim project fiveCounter.circ as structural Verilog: 1 circuit, main circuit fiveCounter
module fiveCounter (
  input  Start,
  input  Clk,
  output S0,
  output S1,
  output S2,
  output S3,
  output S4
);

  D_Flip_Flop d_ff_1 (.D(S4), .clk(Clk), .Q(S0), .preset(Start));  // open: Qn, reset
  D_Flip_Flop d_ff_2 (.D(S0), .clk(Clk), .Q(S1), .reset(Start));  // open: Qn, preset
  D_Flip_Flop d_ff_3 (.D(S1), .clk(Clk), .Q(S2), .reset(Start));  // open: Qn, preset
  D_Flip_Flop d_ff_4 (.D(S2), .clk(Clk), .Q(S3), .reset(Start));  // open: Qn, preset
  D_Flip_Flop d_ff_5 (.D(S3), .clk(Clk), .Q(S4), .reset(Start));  // open: Qn, preset
endmodule
